# Fritzing sketch teleinfo-fritzing (saved by Fritzing 1.0.2b)
breadboards: 1

parts:
  Part1 = Arduino Uno (Rev3) - ICSP
  MH-ET_LIVE_ESP32_DEVKIT1 = MH-ET LIVE ESP32 DEVKIT 38 pins
  U1 = Sharp PC817 [package=THT]
  R1 = Resistor [tolerance=±5% resistance=220 package="0805 [SMD]"]

nets:
  N1: Part1.D1/TX, U1.Pin_2
  N2: Part1.3V3, U1.Pin_1
  N3: MH-ET_LIVE_ESP32_DEVKIT1.3V3, R1.Pin_0
  N4: MH-ET_LIVE_ESP32_DEVKIT1.GND#58, U1.Pin_3
  N5: MH-ET_LIVE_ESP32_DEVKIT1.IO21, U1.Pin_4, R1.Pin_1

custom parts:
  MH-ET LIVE ESP32 DEVKIT 38 pins: http://mh.nodebb.com/topic/2/mh-et-live-esp32-devkit
